// Logisim project CPU2.circ as structural Verilog
module main (
  input  in_1,
  input  in_2,
  input  in_3
);

  wire multiplexer_1_out;

  Multiplexer #(.enable("false")) multiplexer_1 (.in0(in_1), .in1(in_2), .out(multiplexer_1_out), .sel(in_3));
endmodule

module adder (
  input  b,
  input  a,
  input  C_in,
  output A_out,
  output C_out
);

  wire and_1_out, and_2_out, buffer_1_out, or_1_out, xor_1_out, xor_2_out;

  buf buffer_1 (buffer_1_out, C_in);
  and and_1 (and_1_out, a, b);
  xor xor_1 (xor_1_out, b, a);
  xor xor_2 (xor_2_out, xor_1_out, buffer_1_out);
  or or_1 (or_1_out, and_1_out, and_2_out);
  and and_2 (and_2_out, xor_1_out, buffer_1_out);
  buf buffer_2 (C_out, or_1_out);
  buf buffer_3 (A_out, xor_2_out);

  // Notes on the sheet:
  //   Result
endmodule

module _16_adder (
  input  [15:0] B,
  input  [15:0] A,
  output [15:0] out
);

  wire adder_1_c_out, adder_2_c_out, adder_3_c_out, adder_4_c_out, adder_5_c_out, adder_6_c_out,
       adder_7_c_out, adder_8_c_out, adder_9_c_out, adder_10_c_out, adder_11_c_out, adder_12_c_out,
       adder_13_c_out, adder_14_c_out, adder_15_c_out, adder_16_c_out;

  adder adder_1 (.b(B[15]), .a(A[15]), .C_in(adder_2_c_out), .A_out(out[15]), .C_out(adder_1_c_out));
  adder adder_2 (.b(B[14]), .a(A[14]), .C_in(adder_3_c_out), .A_out(out[14]), .C_out(adder_2_c_out));
  adder adder_3 (.b(B[13]), .a(A[13]), .C_in(adder_4_c_out), .A_out(out[13]), .C_out(adder_3_c_out));
  adder adder_4 (.b(B[12]), .a(A[12]), .C_in(adder_5_c_out), .A_out(out[12]), .C_out(adder_4_c_out));
  adder adder_5 (.b(B[11]), .a(A[11]), .C_in(adder_6_c_out), .A_out(out[11]), .C_out(adder_5_c_out));
  adder adder_6 (.b(B[10]), .a(A[10]), .C_in(adder_7_c_out), .A_out(out[10]), .C_out(adder_6_c_out));
  adder adder_7 (.b(B[9]), .a(A[9]), .C_in(adder_8_c_out), .A_out(out[9]), .C_out(adder_7_c_out));
  adder adder_8 (.b(B[8]), .a(A[8]), .C_in(adder_9_c_out), .A_out(out[8]), .C_out(adder_8_c_out));
  adder adder_9 (.b(B[7]), .a(A[7]), .C_in(adder_10_c_out), .A_out(out[7]), .C_out(adder_9_c_out));
  adder adder_10 (.b(B[6]), .a(A[6]), .C_in(adder_11_c_out), .A_out(out[6]), .C_out(adder_10_c_out));
  adder adder_11 (.b(B[5]), .a(A[5]), .C_in(adder_12_c_out), .A_out(out[5]), .C_out(adder_11_c_out));
  adder adder_12 (.b(B[4]), .a(A[4]), .C_in(adder_13_c_out), .A_out(out[4]), .C_out(adder_12_c_out));
  adder adder_13 (.b(B[3]), .a(A[3]), .C_in(adder_14_c_out), .A_out(out[3]), .C_out(adder_13_c_out));
  adder adder_14 (.b(B[2]), .a(A[2]), .C_in(adder_15_c_out), .A_out(out[2]), .C_out(adder_14_c_out));
  adder adder_15 (.b(B[1]), .a(A[1]), .C_in(adder_16_c_out), .A_out(out[1]), .C_out(adder_15_c_out));
  adder adder_16 (.b(B[0]), .a(A[0]), .C_in(1'b0), .A_out(out[0]), .C_out(adder_16_c_out));
endmodule

module _16_twos_compliment (
  input  [15:0] in_1,
  output [15:0] out_2
);

  wire [15:0] not_1_out;

  assign not_1_out = ~in_1;  // NOT_Gate not_1, 16 bits wide
  _16_adder u_16_adder_1 (.B(16'h1), .A(not_1_out), .out(out_2));
endmodule

module ALU (
  input  ADD,
  input  SUB,
  input  MUL,
  input  [15:0] B,
  input  [15:0] A,
  output [15:0] OUT
);

  wire [15:0] n16_adder_1_out, n16_adder_2_out, n16_multiply_1_out_3, n16_twos_compliment_1_out_2;

  _16_twos_compliment u_16_twos_compliment_1 (.in_1(B), .out_2(n16_twos_compliment_1_out_2));
  _16_adder u_16_adder_1 (.B(B), .A(A), .out(n16_adder_1_out));
  _16_adder u_16_adder_2 (.B(n16_twos_compliment_1_out_2), .A(A), .out(n16_adder_2_out));
  _16_multiply u_16_multiply_1 (.in_1(B), .in_2(A), .out_3(n16_multiply_1_out_3));
  assign OUT = ADD ? n16_adder_1_out : 16'bz;  // Controlled_Buffer controlled_buffer_1
  assign OUT = SUB ? n16_adder_2_out : 16'bz;  // Controlled_Buffer controlled_buffer_2
  assign OUT = MUL ? n16_multiply_1_out_3 : 16'bz;  // Controlled_Buffer controlled_buffer_3
endmodule

module _16_Shift_Left (
  input  [15:0] in,
  output [15:0] out
);


  assign out = {in[14:0], 1'b0};
endmodule

module _16_Shift_Right (
  input  [15:0] in,
  output [15:0] out
);


  assign out = {1'b0, in[15:1]};
endmodule

module _1_to_16_duplicator (
  input  in,
  output [15:0] out
);


  assign out = {16{in}};
endmodule

module _16_Least_Significant (
  input  [15:0] in_1,
  output out_2
);


  assign out_2 = in_1[0];
endmodule

module _16_multiply (
  input  [15:0] in_1,
  input  [15:0] in_2,
  output [15:0] out_3
);

  wire [15:0] multiplexer_1_out, multiplexer_2_out, multiplexer_3_out, multiplexer_4_out, multiplexer_5_out,
       multiplexer_6_out, multiplexer_7_out, multiplexer_8_out, multiplexer_9_out, multiplexer_10_out,
       multiplexer_11_out, multiplexer_12_out, multiplexer_13_out, multiplexer_14_out, multiplexer_15_out,
       multiplexer_16_out, n16_adder_1_out, n16_adder_2_out, n16_adder_3_out, n16_adder_4_out,
       n16_adder_5_out, n16_adder_6_out, n16_adder_7_out, n16_adder_9_out, n16_adder_10_out,
       n16_adder_11_out, n16_adder_12_out, n16_adder_13_out, n16_adder_14_out, n16_adder_15_out,
       n16_shift_left_1_out, n16_shift_left_2_out, n16_shift_left_3_out, n16_shift_left_4_out,
       n16_shift_left_5_out, n16_shift_left_6_out, n16_shift_left_7_out, n16_shift_left_8_out,
       n16_shift_left_9_out, n16_shift_left_10_out, n16_shift_left_11_out, n16_shift_left_12_out,
       n16_shift_left_13_out, n16_shift_left_14_out, n16_shift_left_15_out;

  _16_adder u_16_adder_1 (.B(multiplexer_1_out), .A(multiplexer_2_out), .out(n16_adder_1_out));
  Multiplexer #(.width(16), .enable("false")) multiplexer_1 (
    .in0({16{1'b0}}), .in1(in_1), .out(multiplexer_1_out), .sel(in_2[0]));
  _16_Shift_Left u_16_shift_left_1 (.in(in_1), .out(n16_shift_left_1_out));
  _16_adder u_16_adder_2 (.B(n16_adder_1_out), .A(n16_adder_4_out), .out(n16_adder_2_out));
  Multiplexer #(.width(16), .enable("false")) multiplexer_2 (
    .in0({16{1'b0}}), .in1(n16_shift_left_1_out), .out(multiplexer_2_out), .sel(in_2[1]));
  _16_Shift_Left u_16_shift_left_2 (.in(n16_shift_left_1_out), .out(n16_shift_left_2_out));
  _16_adder u_16_adder_3 (.B(n16_adder_2_out), .A(n16_adder_6_out), .out(n16_adder_3_out));
  _16_adder u_16_adder_4 (.B(multiplexer_3_out), .A(multiplexer_4_out), .out(n16_adder_4_out));
  Multiplexer #(.width(16), .enable("false")) multiplexer_3 (
    .in0({16{1'b0}}), .in1(n16_shift_left_2_out), .out(multiplexer_3_out), .sel(in_2[2]));
  Multiplexer #(.width(16), .enable("false")) multiplexer_4 (
    .in0({16{1'b0}}), .in1(n16_shift_left_4_out), .out(multiplexer_4_out), .sel(in_2[3]));
  _16_Shift_Left u_16_shift_left_3 (.in(n16_shift_left_4_out), .out(n16_shift_left_3_out));
  _16_Shift_Left u_16_shift_left_4 (.in(n16_shift_left_2_out), .out(n16_shift_left_4_out));
  _16_adder u_16_adder_5 (.B(multiplexer_5_out), .A(multiplexer_7_out), .out(n16_adder_5_out));
  Multiplexer #(.width(16), .enable("false")) multiplexer_5 (
    .in0({16{1'b0}}), .in1(n16_shift_left_3_out), .out(multiplexer_5_out), .sel(in_2[4]));
  _16_Shift_Left u_16_shift_left_5 (.in(n16_shift_left_3_out), .out(n16_shift_left_5_out));
  _16_adder u_16_adder_6 (.B(n16_adder_5_out), .A(n16_adder_7_out), .out(n16_adder_6_out));
  _16_adder u_16_adder_7 (.B(multiplexer_6_out), .A(multiplexer_8_out), .out(n16_adder_7_out));
  Multiplexer #(.width(16), .enable("false")) multiplexer_6 (
    .in0({16{1'b0}}), .in1(n16_shift_left_6_out), .out(multiplexer_6_out), .sel(in_2[6]));
  Multiplexer #(.width(16), .enable("false")) multiplexer_7 (
    .in0({16{1'b0}}), .in1(n16_shift_left_5_out), .out(multiplexer_7_out), .sel(in_2[5]));
  _16_Shift_Left u_16_shift_left_6 (.in(n16_shift_left_5_out), .out(n16_shift_left_6_out));
  _16_Shift_Left u_16_shift_left_7 (.in(n16_shift_left_6_out), .out(n16_shift_left_7_out));
  _16_adder u_16_adder_8 (.B(n16_adder_3_out), .A(n16_adder_11_out), .out(out_3));
  _16_adder u_16_adder_9 (.B(multiplexer_9_out), .A(multiplexer_10_out), .out(n16_adder_9_out));
  Multiplexer #(.width(16), .enable("false")) multiplexer_8 (
    .in0({16{1'b0}}), .in1(n16_shift_left_7_out), .out(multiplexer_8_out), .sel(in_2[7]));
  Multiplexer #(.width(16), .enable("false")) multiplexer_9 (
    .in0({16{1'b0}}), .in1(n16_shift_left_9_out), .out(multiplexer_9_out), .sel(in_2[8]));
  _16_Shift_Left u_16_shift_left_8 (.in(n16_shift_left_9_out), .out(n16_shift_left_8_out));
  _16_Shift_Left u_16_shift_left_9 (.in(n16_shift_left_7_out), .out(n16_shift_left_9_out));
  _16_adder u_16_adder_10 (.B(n16_adder_9_out), .A(n16_adder_12_out), .out(n16_adder_10_out));
  Multiplexer #(.width(16), .enable("false")) multiplexer_10 (
    .in0({16{1'b0}}), .in1(n16_shift_left_8_out), .out(multiplexer_10_out), .sel(in_2[9]));
  _16_Shift_Left u_16_shift_left_10 (.in(n16_shift_left_8_out), .out(n16_shift_left_10_out));
  _16_adder u_16_adder_11 (.B(n16_adder_10_out), .A(n16_adder_14_out), .out(n16_adder_11_out));
  _16_adder u_16_adder_12 (.B(multiplexer_12_out), .A(multiplexer_11_out), .out(n16_adder_12_out));
  Multiplexer #(.width(16), .enable("false")) multiplexer_11 (
    .in0({16{1'b0}}), .in1(n16_shift_left_12_out), .out(multiplexer_11_out), .sel(in_2[11]));
  Multiplexer #(.width(16), .enable("false")) multiplexer_12 (
    .in0({16{1'b0}}), .in1(n16_shift_left_10_out), .out(multiplexer_12_out), .sel(in_2[10]));
  _16_Shift_Left u_16_shift_left_11 (.in(n16_shift_left_12_out), .out(n16_shift_left_11_out));
  _16_Shift_Left u_16_shift_left_12 (.in(n16_shift_left_10_out), .out(n16_shift_left_12_out));
  _16_adder u_16_adder_13 (.B(multiplexer_13_out), .A(multiplexer_14_out), .out(n16_adder_13_out));
  Multiplexer #(.width(16), .enable("false")) multiplexer_13 (
    .in0({16{1'b0}}), .in1(n16_shift_left_11_out), .out(multiplexer_13_out), .sel(in_2[12]));
  _16_Shift_Left u_16_shift_left_13 (.in(n16_shift_left_11_out), .out(n16_shift_left_13_out));
  _16_adder u_16_adder_14 (.B(n16_adder_13_out), .A(n16_adder_15_out), .out(n16_adder_14_out));
  _16_adder u_16_adder_15 (.B(multiplexer_15_out), .A(multiplexer_16_out), .out(n16_adder_15_out));
  Multiplexer #(.width(16), .enable("false")) multiplexer_14 (
    .in0({16{1'b0}}), .in1(n16_shift_left_13_out), .out(multiplexer_14_out), .sel(in_2[13]));
  Multiplexer #(.width(16), .enable("false")) multiplexer_15 (
    .in0({16{1'b0}}), .in1(n16_shift_left_14_out), .out(multiplexer_15_out), .sel(in_2[14]));
  _16_Shift_Left u_16_shift_left_14 (.in(n16_shift_left_13_out), .out(n16_shift_left_14_out));
  _16_Shift_Left u_16_shift_left_15 (.in(n16_shift_left_14_out), .out(n16_shift_left_15_out));
  Multiplexer #(.width(16), .enable("false")) multiplexer_16 (
    .in0({16{1'b0}}), .in1(n16_shift_left_15_out), .out(multiplexer_16_out), .sel(in_2[15]));
endmodule
